# Fritzing sketch calipers (saved by Fritzing 0.9.3b)

parts:
  Raspberry_Pi = Raspberry Pi 3 [part_number=RPI-3-V1.2]
  BC-548 = NPN-Transistor [package="TO92 [THT]"]
  BC-548_2 = NPN-Transistor [package="TO92 [THT]"]
  R1 = Resistor [tolerance=±5% resistance=10k package=THT]
  R2 = Resistor [tolerance=±5% resistance=10k package=THT]
  R3 = Resistor [tolerance=±5% resistance=10k package=THT]
  R4 = Resistor [tolerance=±5% resistance=10k package=THT]
  Metric/Imperial_Button = Pushbutton [package=THT]
  Speak_Button = Pushbutton [package=THT]

nets (from the schematic view):
  3V3: Raspberry_Pi.3v3, Raspberry_Pi.3V3, R3.Pin_0, R4.Pin_0
  N1: Raspberry_Pi.GPIO3, Speak_Button.leg1
  N2: Raspberry_Pi.GPIO17, R2.Pin_0
  N3: Raspberry_Pi.GPIO27, Metric/Imperial_Button.leg1
  N4: Raspberry_Pi.GND, BC-548.E, BC-548_2.E, Metric/Imperial_Button.leg0, Speak_Button.leg0
  N5: Raspberry_Pi.GPIO18, R1.Pin_0
  N6: BC-548.B, R2.Pin_1
  Caliper Data: BC-548.C, R4.Pin_1
  N7: BC-548_2.B, R1.Pin_1
  Caliper Clock: BC-548_2.C, R3.Pin_1
